# Fritzing sketch wiring sketch (saved by Fritzing 0.9.4)
circuit board: 14.217cm x 10.2687cm
breadboards: 2

parts:
  NANO_Slave = Arduino Nano (Rev3.0)
  MRot = Basic FET N-Channel [package="TO220 [THT]"]
  MGruen = Basic FET P-Channel [package="TO220 [THT]"]
  MBlau = Basic FET P-Channel [package="TO220 [THT]"]
  R1 = Resistor [tolerance=±5% resistance=10k package=THT]
  Bauteil1 = Arduino Uno (Rev3)  # not connected
  LCD1 = elegoo-2.8in-tft-display  # not connected
  +9V = screw terminal, 2 pins
  R2 = Resistor [tolerance=±5% resistance=220 package=THT]
  R3 = Resistor [tolerance=±5% resistance=220 package=THT]
  FAN_C/R = screw terminal, 4 pins
  OUT_RGB = screw terminal, 5 pins
  J1 = screw terminal, 2 pins
  J2 = female pin header, 4 pins [form="♀ (female)"]
  J3 = screw terminal, 4 pins

nets (from the pcb view):
  N1: NANO_Slave.GND, MRot.source, MGruen.source, MBlau.source, +9V.pin2, J2.pin3, J3.pin3
  N2: NANO_Slave.D3, R1.Pin_0, FAN_C/R.pin2
  N3: NANO_Slave.D5, MRot.gate
  N4: NANO_Slave.D6, MGruen.gate
  N5: NANO_Slave.D9, MBlau.gate
  N6: NANO_Slave.D11/MOSI, FAN_C/R.pin1
  N7: NANO_Slave.VIN, +9V.pin1
  N8: NANO_Slave.5V, R1.Pin_1
  N9: NANO_Slave.A5, R3.Pin_1, J3.pin1
  N10: NANO_Slave.A4, R2.Pin_1, J2.pin2
  N11: MRot.drain, OUT_RGB.pin1
  N12: MGruen.drain, OUT_RGB.pin2
  N13: MBlau.drain, OUT_RGB.pin3
  N14: R2.Pin_0, R3.Pin_0
  N15: FAN_C/R.pin3, J1.pin1
  N16: FAN_C/R.pin4, J1.pin2
  N17: J2.pin4, J3.pin4

custom parts:
  elegoo-2.8in-tft-display: 2.8 Inch TFT LCD Touch Screen with SD Card Socket. 240*320 pixels RGB. 4 chip white LED backlight.
